# Fritzing sketch fritzing_template (saved by Fritzing 0.9.10b)
breadboards: 1

parts:
  M5Core-Ink = M5Core-Ink
  Ultrasonic-Sensor = HC-SR04 Ultrasonic Distance Sensor
  元件1 = 12 NeoPixel Ring [part_number=1643]

nets:
  VCC: M5Core-Ink.1_5VIN, Ultrasonic-Sensor.VCC, 元件1.VDD
  GND: M5Core-Ink.8_GND, Ultrasonic-Sensor.GND, 元件1.GND
  N1: M5Core-Ink.13_G25, Ultrasonic-Sensor.ECHO
  N2: M5Core-Ink.14_G23, Ultrasonic-Sensor.TRIG
  N3: M5Core-Ink.15_G26, 元件1.IN

custom parts:
  M5Core-Ink: M5Stack Core Ink ESP32 Board
  12 NeoPixel Ring: 12 ultra bright smart LED NeoPixels are arranged in a circle with 1.5" (37mm) outer diameter. The rings are 'chainable' - connect the output pin of one to the input pin of another. Use only one microcontroller pin to control as many as you can chain together! Each LED is addressable as the driver chip is inside the LED. Each one has ~18mA constant current drive so the color will be very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
